// Logisim project Basic4Bit.circ as structural Verilog: 1 circuit, main circuit main
module main (
  input  [7:0] in_1
);

  wire A, A_pin1, A_pin7, A_pin9, A_pin10, ADD, adder_1_cout, ALU_pin1, ALU_pin7, ALU_pin9, ALU_pin10,
       and_1_out, and_2_out, and_3_out, and_4_out, and_5_out, and_6_out, and_7_out, B, B_pin1, B_pin7,
       B_pin9, B_pin10, C_q, CLK, CMP, EX, FD, IncPC, instNAND, JPC, JPZ, LDI, LDST, n74138_1_pin4,
       n74138_1_pin5, n74138_1_pin6, nand_1_out, not_1_out, not_2_out, not_3_out, not_4_out, not_5_out,
       not_6_out, not_7_out, not_8_out, PCH_pin1, PCH_pin2, PCH_pin7, PCH_pin10, PCL_pin1, PCL_pin7,
       PCL_pin10, PT, ST, WPCH, WPCL;
  wire [1:0] counter_1_q;
  wire [2:0] INST;
  wire [3:0] adder_1_out, ALUOUT, AOUT, BOUT, controlled_buffer_3_out, controlled_buffer_9_out,
       controlled_buffer_10_out, DATA, nand_2_out, PCH_pin14, PCL_pin14;
  wire [7:0] ADDRESS, PCH_pin3;
  wire [7:4] DataBuffer_q;

  // DipSwitch Start: pin names not known
  Counter #(.max('h3), .trigger("falling"), .width(2)) counter_1 (
    .clk(CLK), .Q(counter_1_q));  // open: clr, load, up, count, D, carry
  _74161 #(.ShowInternalStructure("true")) PCH (
    .pin1(PCH_pin1), .pin2(PCH_pin2), .pin3(PCH_pin3[0]), .pin4(PCH_pin3[1]), .pin5(PCH_pin3[2]),
    .pin6(PCH_pin3[3]), .pin7(PCH_pin7), .pin14(PCH_pin14[0]), .pin13(PCH_pin14[1]), .pin12(PCH_pin14[2]),
    .pin11(PCH_pin14[3]), .pin10(PCH_pin10), .pin9(WPCH));  // open: pin15
  _74161 #(.ShowInternalStructure("true")) PCL (
    .pin1(PCL_pin1), .pin2(IncPC), .pin3(PCH_pin3[4]), .pin4(PCH_pin3[5]), .pin5(PCH_pin3[6]),
    .pin6(PCH_pin3[7]), .pin7(PCL_pin7), .pin15(PCH_pin2), .pin14(PCL_pin14[0]), .pin13(PCL_pin14[1]),
    .pin12(PCL_pin14[2]), .pin11(PCL_pin14[3]), .pin10(PCL_pin10), .pin9(WPCL));
  not not_1 (not_1_out, LDST);
  and and_1 (and_1_out, CLK, not_1_out, ST);
  and and_2 (and_2_out, FD, CLK);
  Demultiplexer #(.select(2)) demultiplexer_1 (
    .out0(FD), .out1(EX), .out2(ST), .out3(IncPC), .in(1'b1), .sel(counter_1_q));
  Clock clock_1 (.out(CLK));
  RAM #(.trigger("falling"), .\type ("nonvolatile")) FRAM (
    .addr(ADDRESS), .we(and_1_out), .oe(and_2_out), .clk(CLK));  // open: din, dout
  // Probe on INST
  // Probe on B
  // Probe on DATA
  assign ADDRESS = not_2_out ? {PCH_pin14, PCL_pin14} : 8'bz;  // Controlled_Buffer controlled_buffer_1
  not not_2 (not_2_out, not_3_out);
  assign ADDRESS = not_3_out ? {4'b1111, BOUT} : 8'bz;  // Controlled_Buffer controlled_buffer_2
  not not_3 (not_3_out, LDST);
  Pull_Resistor pull_resistor_1 (.node(ADDRESS));
  not not_4 (not_4_out, ST);
  _74161 #(.ShowInternalStructure("true")) u_A (
    .pin1(A_pin1), .pin2(not_4_out), .pin3(DATA[0]), .pin4(DATA[1]), .pin5(DATA[2]), .pin6(DATA[3]),
    .pin7(A_pin7), .pin14(AOUT[0]), .pin13(AOUT[1]), .pin12(AOUT[2]), .pin11(AOUT[3]), .pin10(A_pin10),
    .pin9(A_pin9));  // open: pin15
  or or_1 (A_pin9, ST, B, and_3_out);
  and and_3 (and_3_out, LDI, LDST, PT);
  Register DataBuffer (.D(in_1), .en(FD), .clk(CLK), .Q({DataBuffer_q, B, INST}));  // open: clr
  assign controlled_buffer_3_out = not_5_out ? DATA : 4'bz;  // Controlled_Buffer controlled_buffer_3
  not not_5 (not_5_out, B);
  assign controlled_buffer_3_out = B ? BOUT : 4'bz;  // Controlled_Buffer controlled_buffer_4
  assign DATA = not_6_out ? DataBuffer_q : 4'bz;  // Controlled_Buffer controlled_buffer_5
  not not_6 (not_6_out, and_6_out);
  not not_7 (not_7_out, PT);
  and and_4 (and_4_out, not_7_out, B);
  and and_5 (and_5_out, not_7_out, A);
  and and_6 (and_6_out, ST, nand_1_out);
  nand nand_1 (nand_1_out, ADD, instNAND);
  _74161 #(.ShowInternalStructure("true")) u_B (
    .pin1(B_pin1), .pin2(ST), .pin3(DATA[0]), .pin4(DATA[1]), .pin5(DATA[2]), .pin6(DATA[3]), .pin7(B_pin7),
    .pin14(BOUT[0]), .pin13(BOUT[1]), .pin12(BOUT[2]), .pin11(BOUT[3]), .pin10(B_pin10), .pin9(B_pin9));  // open: pin15
  and and_7 (and_7_out, LDI, PT);
  or or_2 (B_pin9, and_7_out, A);
  D_Flip_Flop C (.D(adder_1_cout), .clk(ADD), .Q(C_q));  // open: Qn, preset, reset
  assign DATA = and_4_out ? AOUT : 4'bz;  // Controlled_Buffer controlled_buffer_6
  assign DATA = and_5_out ? BOUT : 4'bz;  // Controlled_Buffer controlled_buffer_7
  assign DATA = and_6_out ? ALUOUT : 4'bz;  // Controlled_Buffer controlled_buffer_8
  Adder #(.width(4)) adder_1 (.a(controlled_buffer_3_out), .b(AOUT), .out(adder_1_out), .cin(C_q), .cout(adder_1_cout));
  assign controlled_buffer_9_out = not_5_out ? AOUT : 4'bz;  // Controlled_Buffer controlled_buffer_9
  assign controlled_buffer_10_out = instNAND ? adder_1_out : 4'bz;  // Controlled_Buffer controlled_buffer_10
  not not_8 (not_8_out, instNAND);
  assign nand_2_out = ~(AOUT & controlled_buffer_9_out);  // NAND_Gate nand_2, 4 bits wide
  assign controlled_buffer_10_out = not_8_out ? nand_2_out : 4'bz;  // Controlled_Buffer controlled_buffer_11
  _74161 #(.ShowInternalStructure("true")) ALU (
    .pin1(ALU_pin1), .pin2(EX), .pin3(controlled_buffer_10_out[0]), .pin4(controlled_buffer_10_out[1]),
    .pin5(controlled_buffer_10_out[2]), .pin6(controlled_buffer_10_out[3]), .pin7(ALU_pin7),
    .pin14(ALUOUT[0]), .pin13(ALUOUT[1]), .pin12(ALUOUT[2]), .pin11(ALUOUT[3]), .pin10(ALU_pin10),
    .pin9(ALU_pin9));  // open: pin15
  and and_8 (ALU_pin9, ADD, instNAND);
  _74138 #(.ShowInternalStructure("true")) u_74138_1 (
    .pin1(INST[0]), .pin2(INST[1]), .pin3(INST[2]), .pin4(n74138_1_pin4), .pin5(n74138_1_pin5),
    .pin6(n74138_1_pin6), .pin7(JPC), .pin15(LDI), .pin14(PT), .pin13(ADD), .pin12(instNAND), .pin11(LDST),
    .pin10(CMP), .pin9(JPZ));
  _7414 #(.ShowInternalStructure("true")) u_7414_1 (
    .pin13(B), .pin12(A));  // open: pin1, pin2, pin3, pin4, pin5, pin6, pin11, pin10, pin9, pin8
  _7400 #(.ShowInternalStructure("true")) u_7400_1 ();  // open: pin1, pin2, pin3, pin4, pin5, pin6, pin13, pin12, pin11, pin10, pin9, pin8
  // also tied to GND on the sheet: {A_pin7, A_pin10, B_pin7, B_pin10, ALU_pin7, n74138_1_pin4, n74138_1_pin5, ALU_pin10}
  // also tied to VCC on the sheet: {PCH_pin1, PCH_pin7, PCL_pin1, PCL_pin7, PCH_pin10, PCL_pin10, A_pin1, B_pin1, ALU_pin1, n74138_1_pin6}

  // Other names for the same wires on the sheet: nA = B; DATAEXT[7:0] = in_1; nB = A

  // Notes on the sheet:
  //   the most jank way to do this, would be using the first two bits of PC for this
  //   Registers
endmodule
