// Logisim project BeFour.circ as structural Verilog: 1 circuit, main circuit main
module main (
  input  [7:0] in_1
);

  wire A_pin7, A_pin10, AB, ADD, adder_1_cout, ADDRESSING, Addressing_t, ALUOP, and_2_out, and_5_out,
       and_6_out, B_pin7, B_pin10, C_q, CLK, CMP, INCPC, INST_pin1, INST_pin11, instNAND, JP, JPC, LD, LDI,
       LDINST, n74138_1_pin3, n74138_1_pin5, n74138_1_pin6, n74138_2_pin4, n74138_2_pin5, n74138_2_pin6,
       n74161_1_pin7, n74161_1_pin9, n74161_1_pin10, n74161_1_pin13, n74161_1_pin14, nAB, nCLK, nor_1_out,
       not_4_out, not_5_out, not_6_out, not_7_out, not_8_out, not_9_out, not_11_out, not_12_out, not_13_out,
       not_14_out, not_15_out, not_16_out, not_17_out, not_18_out, not_19_out, not_20_out, not_21_out,
       not_22_out, nRESET, OP1, OP2, OPERATION, or_1_out, or_3_out, outputA, outputB, outputLiveImm,
       outputTemp, PCH_pin2, PCH_pin7, PCH_pin9, PCH_pin10, PCL_pin2, PCL_pin7, PCL_pin9, PCL_pin10, RESET,
       ST, TEMP_pin7, TEMP_pin10, wrA, wrB;
  wire [2:0] INST;
  wire [3:0] adder_1_out, AOUT, BOUT, controlled_buffer_3_out, DATABUS, LiveImmediate, nand_1_out, PCH_pin14,
       PCL_pin14, StoredImmediate, TEMPIN, TEMPOUT;
  wire [7:0] ADDRESS, DATA, PCH_pin3;
  wire [7:4] buffer_1_out;

  Clock clock_1 (.out(CLK));
  // DipSwitch Start: pin names not known
  POR #(.PorHighDuration(1)) por_1 (.out(RESET));
  not not_1 (nCLK, CLK);
  _74161 #(.ShowInternalStructure("true")) PCH (
    .pin1(nRESET), .pin2(PCH_pin2), .pin3(PCH_pin3[0]), .pin4(PCH_pin3[1]), .pin5(PCH_pin3[2]),
    .pin6(PCH_pin3[3]), .pin7(PCH_pin7), .pin14(PCH_pin14[0]), .pin13(PCH_pin14[1]), .pin12(PCH_pin14[2]),
    .pin11(PCH_pin14[3]), .pin10(PCH_pin10), .pin9(PCH_pin9));  // open: pin15
  _74161 #(.ShowInternalStructure("true")) PCL (
    .pin1(nRESET), .pin2(PCL_pin2), .pin3(PCH_pin3[4]), .pin4(PCH_pin3[5]), .pin5(PCH_pin3[6]),
    .pin6(PCH_pin3[7]), .pin7(PCL_pin7), .pin15(PCH_pin2), .pin14(PCL_pin14[0]), .pin13(PCL_pin14[1]),
    .pin12(PCL_pin14[2]), .pin11(PCL_pin14[3]), .pin10(PCL_pin10), .pin9(PCL_pin9));
  not not_2 (PCL_pin2, INCPC);
  or or_1 (or_1_out, ST, OPERATION);
  not not_3 (nRESET, RESET);
  RAM #(.asyncread("true"), .databus("bidir"), .\type ("nonvolatile")) ram_1 (
    .addr(ADDRESS), .we(not_4_out), .oe(or_1_out), .clk(nCLK), .data(DATA));
  not not_4 (not_4_out, or_1_out);
  assign ADDRESS = not_5_out ? {PCH_pin14, PCL_pin14} : 8'bz;  // Controlled_Buffer controlled_buffer_1
  not not_5 (not_5_out, Addressing_t);
  assign ADDRESS = Addressing_t ? {4'b1111, StoredImmediate} : 8'bz;  // Controlled_Buffer controlled_buffer_2
  _74125 #(.ShowInternalStructure("true")) u_74125_1 ();  // open: pin1, pin2, pin3, pin4, pin5, pin6, pin13, pin12, pin11, pin10, pin9, pin8
  _74161 #(.ShowInternalStructure("true")) u_74161_1 (
    .pin1(nRESET), .pin2(nCLK), .pin7(n74161_1_pin7), .pin14(n74161_1_pin14), .pin13(n74161_1_pin13),
    .pin10(n74161_1_pin10), .pin9(n74161_1_pin9));  // open: pin3, pin4, pin5, pin6, pin15, pin12, pin11
  Pull_Resistor pull_resistor_1 (.node(ADDRESS));
  Hex_Digit_Display #(.decimalPoint("false")) hex_digit_display_1 (.value(AOUT));
  Hex_Digit_Display #(.decimalPoint("false")) hex_digit_display_2 (.value({3'b101, AB}));
  Hex_Digit_Display #(.decimalPoint("false")) hex_digit_display_3 (.value(DATABUS));
  // Probe on DATA
  Hex_Digit_Display #(.decimalPoint("false")) hex_digit_display_4 (.value(BOUT));
  Hex_Digit_Display #(.decimalPoint("false")) hex_digit_display_5 (.value(ADDRESS[7:4]));
  Hex_Digit_Display #(.decimalPoint("false")) hex_digit_display_6 (.value({1'b0, INST}));
  _74138 #(.ShowInternalStructure("true")) u_74138_1 (
    .pin1(n74161_1_pin14), .pin2(n74161_1_pin13), .pin3(n74138_1_pin3), .pin4(RESET), .pin5(n74138_1_pin5),
    .pin6(n74138_1_pin6), .pin15(LDINST), .pin14(OP1), .pin13(OP2), .pin12(INCPC));  // open: pin7, pin11, pin10, pin9
  Hex_Digit_Display #(.decimalPoint("false")) hex_digit_display_7 (.value(ADDRESS[3:0]));
  Hex_Digit_Display #(.decimalPoint("false")) hex_digit_display_8 (.value(TEMPOUT));
  _74161 #(.ShowInternalStructure("true")) A (
    .pin1(nRESET), .pin2(CLK), .pin3(DATABUS[0]), .pin4(DATABUS[1]), .pin5(DATABUS[2]), .pin6(DATABUS[3]),
    .pin7(A_pin7), .pin14(AOUT[0]), .pin13(AOUT[1]), .pin12(AOUT[2]), .pin11(AOUT[3]), .pin10(A_pin10),
    .pin9(wrA));  // open: pin15
  and and_1 (OPERATION, OP1, OP2);
  _74161 #(.ShowInternalStructure("true")) B (
    .pin1(nRESET), .pin2(CLK), .pin3(DATABUS[0]), .pin4(DATABUS[1]), .pin5(DATABUS[2]), .pin6(DATABUS[3]),
    .pin7(B_pin7), .pin14(BOUT[0]), .pin13(BOUT[1]), .pin12(BOUT[2]), .pin11(BOUT[3]), .pin10(B_pin10),
    .pin9(wrB));  // open: pin15
  D_Flip_Flop C (.D(adder_1_cout), .clk(ADD), .Q(C_q));  // open: Qn, preset, reset
  Adder #(.width(4)) adder_1 (.a(DATABUS), .b(AOUT), .out(adder_1_out), .cin(C_q), .cout(adder_1_cout));
  not not_6 (not_6_out, ALUOP);
  assign controlled_buffer_3_out = instNAND ? adder_1_out : 4'bz;  // Controlled_Buffer controlled_buffer_3
  not not_7 (not_7_out, instNAND);
  assign nand_1_out = ~(AOUT & DATABUS);  // NAND_Gate nand_1, 4 bits wide
  assign controlled_buffer_3_out = not_7_out ? nand_1_out : 4'bz;  // Controlled_Buffer controlled_buffer_4
  not not_8 (not_8_out, INST[1]);
  not not_9 (not_9_out, INST[0]);
  assign TEMPIN = not_6_out ? controlled_buffer_3_out : 4'bz;  // Controlled_Buffer controlled_buffer_5
  or or_2 (wrB, OP2, or_3_out);
  or or_3 (or_3_out, LDI, nAB);
  and and_2 (and_2_out, AB, not_8_out, not_9_out);
  assign {buffer_1_out, LiveImmediate} = DATA;  // Buffer buffer_1, 8 bits wide
  Pull_Resistor pull_resistor_2 (.node(buffer_1_out));
  or or_4 (wrA, INST[2], and_2_out, OP2);
  Pull_Resistor pull_resistor_3 (.node(TEMPIN));
  _74161 #(.ShowInternalStructure("true")) TEMP (
    .pin1(nRESET), .pin2(OP1), .pin3(TEMPIN[0]), .pin4(TEMPIN[1]), .pin5(TEMPIN[2]), .pin6(TEMPIN[3]),
    .pin7(TEMP_pin7), .pin14(TEMPOUT[0]), .pin13(TEMPOUT[1]), .pin12(TEMPOUT[2]), .pin11(TEMPOUT[3]),
    .pin10(TEMP_pin10), .pin9(ALUOP));  // open: pin15
  _74377 #(.ShowInternalStructure("true")) u_INST (
    .pin1(INST_pin1), .pin2(INST[0]), .pin3(LiveImmediate[0]), .pin4(LiveImmediate[1]), .pin5(INST[1]),
    .pin6(INST[2]), .pin7(LiveImmediate[2]), .pin8(LiveImmediate[3]), .pin9(AB), .pin19(StoredImmediate[3]),
    .pin18(buffer_1_out[7]), .pin17(buffer_1_out[6]), .pin16(StoredImmediate[2]), .pin15(StoredImmediate[1]),
    .pin14(buffer_1_out[5]), .pin13(buffer_1_out[4]), .pin12(StoredImmediate[0]), .pin11(INST_pin11));
  not not_10 (INST_pin11, LDINST);
  not not_11 (not_11_out, ST);
  not not_12 (not_12_out, OPERATION);
  not not_13 (not_13_out, ST);
  not not_14 (not_14_out, OPERATION);
  not not_15 (not_15_out, ALUOP);
  not not_16 (not_16_out, OP1);
  not not_17 (not_17_out, ALUOP);
  and and_3 (outputTemp, not_17_out, not_18_out);
  not not_18 (not_18_out, OP2);
  not not_19 (not_19_out, ADDRESSING);
  not not_20 (not_20_out, OPERATION);
  and and_4 (outputA, not_11_out, nAB, not_12_out);
  // Probe on outputA
  and and_5 (and_5_out, not_13_out, AB, not_14_out);
  and and_6 (and_6_out, not_15_out, AB, not_16_out);
  and and_7 (Addressing_t, not_19_out, not_20_out);
  not not_21 (not_21_out, LD);
  and and_8 (outputLiveImm, not_21_out, not_22_out);
  not not_22 (not_22_out, OPERATION);
  or or_5 (outputB, and_5_out, and_6_out);
  // Probe on outputB
  assign DATABUS = nor_1_out ? StoredImmediate : 4'bz;  // Controlled_Buffer controlled_buffer_6
  nor nor_1 (nor_1_out, outputLiveImm, outputB, outputA, outputTemp);
  assign DATABUS = outputLiveImm ? LiveImmediate : 4'bz;  // Controlled_Buffer controlled_buffer_7
  assign DATABUS = outputB ? AOUT : 4'bz;  // Controlled_Buffer controlled_buffer_8
  assign DATABUS = outputA ? BOUT : 4'bz;  // Controlled_Buffer controlled_buffer_9
  assign DATABUS = outputTemp ? TEMPOUT : 4'bz;  // Controlled_Buffer controlled_buffer_10
  _74138 #(.ShowInternalStructure("true")) u_74138_2 (
    .pin1(INST[0]), .pin2(INST[1]), .pin3(INST[2]), .pin4(n74138_2_pin4), .pin5(n74138_2_pin5),
    .pin6(n74138_2_pin6), .pin7(JPC), .pin15(LDI), .pin14(LD), .pin13(ADD), .pin12(instNAND), .pin11(CMP),
    .pin10(ST), .pin9(JP));
  not not_23 (nAB, AB);
  and and_9 (ALUOP, ADD, instNAND);
  and and_10 (ADDRESSING, LD, ST);
  // also tied to GND on the sheet: {n74138_1_pin3, n74138_1_pin5, A_pin7, A_pin10, B_pin7, B_pin10, INST_pin1, TEMP_pin7, TEMP_pin10, n74138_2_pin4, n74138_2_pin5}
  // also tied to VCC on the sheet: {PCH_pin7, PCL_pin7, PCH_pin10, PCH_pin9, PCL_pin10, PCL_pin9, n74161_1_pin7, n74161_1_pin10, n74161_1_pin9, n74138_1_pin6, n74138_2_pin6}

  // Other names for the same wires on the sheet: DATAEXTMANUAL[7:0] = in_1;
  //   StoredInstruction[7:0] = {StoredImmediate, AB, INST}

  // Notes on the sheet:
  //   in_1: initial=0x4
  //   Registers
endmodule
